# Fritzing sketch Level 1 motor stage (saved by Fritzing 0.9.9b)
breadboards: 2

parts:
  Part1 = Arduino Mega 2560 (Rev3)
  S1 = H-Bridge with L298N
  M1 = DC Motor  # not connected
  M2 = DC Motor  # not connected
  M3 = DC Motor  # not connected
  M4 = DC Motor  # not connected
  VCC1 = Battery block 9V
  Buck_Convertor1 = Buck Convertor [part_number=LM2596 package=THT]

nets (from the breadboard view):
  N1: Part1.GND, VCC1.-, Buck_Convertor1.Negative_Input
  N2: Part1.VIN, VCC1.+, Buck_Convertor1.Positive_Input
  N3: Part1.D4_PWM, S1.ENA
  N4: Part1.D5_PWM, S1.ENB
  N5: Part1.D22, S1.IN4
  N6: Part1.D24, S1.IN3
  N7: Part1.D26, S1.IN2
  N8: Part1.D28, S1.IN1
  N9: S1.12V, Buck_Convertor1.Positive_Output
  N10: S1.GND, Buck_Convertor1.Negative_Output

notes:
  Level 1 of Motor Stage

custom parts:
  H-Bridge with L298N: h-bridge
  Buck Convertor: DC to DC buck convertor
